// Logisim project de_6_faces.circ as structural Verilog: 2 circuits, main circuit dé 6 faces
module main (
  input  in_1,
  output out_2,
  output out_3,
  output out_4,
  output out_5,
  output out_6,
  output out_7,
  output out_8
);

  wire random_1_out, random_2_out, random_3_out;

  Random #(.width(1)) random_1 (.clk(in_1), .out(random_1_out));  // open: next, clr
  Random #(.width(1)) random_2 (.clk(in_1), .out(random_2_out));  // open: next, clr
  Random #(.width(1)) random_3 (.out(random_3_out));  // open: clk, next, clr
  \dé_6_faces  \Dé_6_faces  (
    .x(random_1_out), .y(random_2_out), .z(random_3_out), .a(out_3), .b(out_2), .c(out_4), .d(out_6),
    .e(out_5), .f(out_7), .g(out_8));
endmodule

module \dé_6_faces  (
  input  x,
  input  y,
  input  z,
  output a,
  output b,
  output c,
  output d,
  output e,
  output f,
  output g
);

  wire and_1_out, and_2_out, and_3_out, and_4_out, and_5_out, and_6_out, and_8_out, and_9_out, and_11_out,
       and_12_out, and_13_out, and_14_out, and_15_out, and_16_out, not_1_out, not_2_out, not_3_out,
       not_4_out, not_5_out, not_6_out, not_7_out, not_8_out, not_9_out, not_10_out, not_11_out, not_12_out,
       not_13_out, not_14_out, or_1_out, or_5_out;

  Random random_1 ();  // open: clk, next, out, clr
  not not_1 (not_1_out, x);
  not not_2 (not_2_out, y);
  not not_3 (not_3_out, y);
  not not_4 (not_4_out, z);
  and and_1 (and_1_out, x, y);
  not not_5 (not_5_out, z);
  not not_6 (not_6_out, x);
  not not_7 (not_7_out, y);
  and and_2 (and_2_out, x, y);
  not not_8 (not_8_out, z);
  not not_9 (not_9_out, y);
  not not_10 (not_10_out, z);
  not not_11 (not_11_out, x);
  not not_12 (not_12_out, y);
  and and_3 (and_3_out, not_1_out, y);
  and and_4 (and_4_out, x, not_2_out);
  not not_13 (not_13_out, z);
  and and_5 (and_5_out, x, not_3_out);
  and and_6 (and_6_out, x, not_4_out);
  and and_7 (c, and_1_out, not_5_out);
  and and_8 (and_8_out, not_6_out, z);
  and and_9 (and_9_out, not_7_out, z);
  and and_10 (e, and_2_out, not_8_out);
  and and_11 (and_11_out, x, not_9_out);
  and and_12 (and_12_out, x, not_10_out);
  and and_13 (and_13_out, not_11_out, y);
  and and_14 (and_14_out, x, not_12_out);
  not not_14 (not_14_out, z);
  or or_1 (or_1_out, and_3_out, and_4_out);
  and and_15 (and_15_out, x, not_13_out);
  or or_2 (b, and_5_out, and_6_out);
  or or_3 (d, and_8_out, and_9_out);
  or or_4 (f, and_11_out, and_12_out);
  or or_5 (or_5_out, and_13_out, and_14_out);
  and and_16 (and_16_out, x, not_14_out);
  or or_6 (a, or_1_out, and_15_out);
  or or_7 (g, or_5_out, and_16_out);
endmodule
